# Fritzing sketch HomePi (saved by Fritzing 0.9.2b)
breadboards: 1

parts:
  DHT1 = DHT11 Humitidy and Temperature Sensor
  Часть1 = HC-SR501 Body Sensor Module
  R1 = Resistor [tolerance=±5% resistance=4.7k package="2512 [SMD]"]
  Raspberry_Pi_1 = Raspberry Pi 3
  R2 = Resistor [tolerance=±5% resistance=270 package="1206 [SMD]"]
  LED1 = LEDs [package=led10mm]
  LED2 = LEDs [package=led10mm]
  LED3 = LEDs [package=led10mm]
  LED4 = LEDs [package=led10mm]
  R3 = Resistor [tolerance=±5% resistance=270 package="1206 [SMD]"]
  R4 = Resistor [tolerance=±5% resistance=270 package="1206 [SMD]"]
  R5 = Resistor [tolerance=±5% resistance=270 package="1206 [SMD]"]

nets:
  VDD: DHT1.VDD, Часть1.OUT, R1.Pin_0, Raspberry_Pi_1.5V
  N1: DHT1.DATA, R1.Pin_1, Raspberry_Pi_1.GIPO17
  GND: DHT1.GND, Часть1.GND, Raspberry_Pi_1.GND, R2.Pin_0, R3.Pin_0, R4.Pin_0, R5.Pin_0
  N2: Часть1.VCC, Raspberry_Pi_1.GIPO21
  N3: Raspberry_Pi_1.GIPO6, LED1.A
  N4: Raspberry_Pi_1.GIPO13, LED2.A
  N5: Raspberry_Pi_1.GIPO19, LED3.A
  N6: Raspberry_Pi_1.GIPO26, LED4.A
  N7: R2.Pin_1, LED1.C
  N8: LED2.C, R4.Pin_1
  N9: LED3.C, R5.Pin_1
  N10: LED4.C, R3.Pin_1

custom parts:
  DHT11 Humitidy and Temperature Sensor: DHT11 Humidity and Temperature Sensor
  HC-SR501 Body Sensor Module: Pyroelectric Infrared PIR Motion Sensor Detector Module
